// Logisim project activity_1.circ as structural Verilog: 9 circuits, main circuit main
module main (
  input  A,
  input  B,
  input  C,
  output F,
  output G
);

  a_NAND a_nand_1 (.A(A), .B(B), .C(C), .F(F));
  b_NAND b_nand_1 (.A(A), .B(B), .C(C), .G(G));
  LED led_1 (.in(G));
endmodule

module a_NAND (
  input  A,
  input  B,
  input  C,
  output F
);

  wire nand_1_out, nand_2_out, nand_3_out;

  nand nand_1 (nand_1_out, A, B);
  nand nand_2 (nand_2_out, A, C);
  nand nand_3 (nand_3_out, B, C);
  nand nand_4 (F, nand_1_out, nand_2_out, nand_3_out);
endmodule

module b_NAND (
  input  A,
  input  B,
  input  C,
  output G
);

  wire nand_1_out, nand_2_out, nand_3_out, nand_4_out, nand_5_out, nand_6_out;

  nand nand_1 (nand_1_out, B, B);
  nand nand_2 (nand_2_out, A, A);
  nand nand_3 (nand_3_out, C, C);
  nand nand_4 (nand_4_out, A, nand_1_out);
  nand nand_5 (nand_5_out, nand_2_out, C);
  nand nand_6 (nand_6_out, B, nand_3_out);
  nand nand_7 (G, nand_4_out, nand_5_out, nand_6_out);
endmodule

module a_NOR (
  input  A,
  input  B,
  input  C,
  output F
);

  wire nor_1_out, nor_2_out, nor_3_out;

  nor nor_1 (nor_1_out, A, B);
  nor nor_2 (nor_2_out, A, C);
  nor nor_3 (nor_3_out, B, C);
  nor nor_4 (F, nor_1_out, nor_2_out, nor_3_out);
endmodule

module b_NOR (
  input  A,
  input  B,
  input  C,
  output G
);

  wire nor_1_out, nor_2_out, nor_3_out, nor_4_out, nor_5_out;

  nor nor_1 (nor_1_out, A, A);
  nor nor_2 (nor_2_out, B, B);
  nor nor_3 (nor_3_out, C, C);
  nor nor_4 (nor_4_out, A, B, C);
  nor nor_5 (nor_5_out, nor_1_out, nor_2_out, nor_3_out);
  nor nor_6 (G, nor_4_out, nor_5_out);
endmodule

module a_SOP (
  input  A,
  input  B,
  input  C,
  output F
);

  wire and_1_out, and_2_out, and_3_out;

  and and_1 (and_1_out, A, B);
  and and_2 (and_2_out, A, C);
  and and_3 (and_3_out, B, C);
  or or_1 (F, and_1_out, and_2_out, and_3_out);
endmodule

module a_POS (
  input  A,
  input  B,
  input  C,
  output F
);

  wire or_1_out, or_2_out, or_3_out;

  or or_1 (or_1_out, A, B);
  or or_2 (or_2_out, A, C);
  or or_3 (or_3_out, B, C);
  and and_1 (F, or_1_out, or_2_out, or_3_out);
endmodule

module b_SOP (
  input  A,
  input  B,
  input  C,
  output G
);

  wire and_1_out, and_2_out, and_3_out;

  and and_1 (and_1_out, A, ~B);  // AND_Gate
  and and_2 (and_2_out, ~A, C);  // AND_Gate
  and and_3 (and_3_out, B, ~C);  // AND_Gate
  or or_1 (G, and_1_out, and_2_out, and_3_out);
endmodule

module b_POS (
  input  A,
  input  B,
  input  C,
  output G
);

  wire or_1_out, or_2_out;

  or or_1 (or_1_out, A, B, C);
  or or_2 (or_2_out, ~A, ~B, ~C);  // OR_Gate
  and and_1 (G, or_1_out, or_2_out);
endmodule
