// Logisim project activity_2.circ as structural Verilog: 1 circuit, main circuit main
module main (
  input  A,
  input  B,
  input  C,
  output L1,
  output L2,
  output L3,
  output L4,
  output L5
);

  wire nand_1_out, nand_2_out, nand_3_out, nand_4_out, nand_5_out, nand_6_out, nand_7_out, nand_8_out,
       nand_9_out;

  nand nand_1 (nand_1_out, 1'b1, C);
  nand nand_2 (nand_2_out, 1'b1, B);
  nand nand_3 (nand_3_out, 1'b1, A);
  nand nand_4 (nand_4_out, 1'b1, B);
  nand nand_5 (nand_5_out, 1'b1, A);
  nand nand_6 (nand_6_out, B, C);
  nand nand_7 (nand_7_out, 1'b1, A);
  nand nand_8 (nand_8_out, A, C);
  nand nand_9 (nand_9_out, A, C);
  nand nand_10 (L1, nand_1_out, nand_2_out, nand_3_out);
  nand nand_11 (L2, nand_4_out, nand_5_out);
  nand nand_12 (L3, nand_6_out, nand_7_out);
  nand nand_13 (L5, nand_8_out, nand_9_out);

  assign L4 = A;
endmodule
