// Logisim project 7seg.circ as structural Verilog: 4 circuits, main circuit main
module main (
  input  in_1,
  input  in_2,
  input  in_3,
  input  in_4
);

  wire a, b;

  a a_1 (.B3(in_1), .B2(in_2), .B1(in_3), .B0(in_4), .a_out(a));
  b b_1 (.B1(in_3), .B0(in_4), .B2(in_2), .b_out(b));

  // Other names for the same wires on the sheet: B0 = in_4; B1 = in_3; B2 = in_2; B3 = in_1
endmodule

module a (
  input  B3,
  input  B2,
  input  B1,
  input  B0,
  output a_out
);

  wire and_1_out, not_1_out, or_1_out;

  not not_1 (not_1_out, B1);
  and and_1 (and_1_out, B3, not_1_out);
  or or_1 (or_1_out, B2, B0);
  or or_2 (a_out, or_1_out, B1, and_1_out);
endmodule

module b (
  input  B1,
  input  B0,
  input  B2,
  output b_out
);

  wire not_1_out, xnor_1_out;

  xnor xnor_1 (xnor_1_out, B1, B0);
  not not_1 (not_1_out, B2);
  or or_1 (b_out, xnor_1_out, not_1_out);
endmodule

module c (
  input  in_1
);
endmodule
