// Logisim project Adders.circ as structural Verilog
module FA (
  input  X,
  input  Y,
  input  C_i,
  output C_o,
  output S
);

  wire and_1_out, and_2_out, and_3_out, and_4_out, and_5_out, and_6_out, and_7_out, not_1_out, not_2_out,
       not_3_out;

  not not_1 (not_1_out, C_i);
  not not_2 (not_2_out, X);
  not not_3 (not_3_out, Y);
  and and_1 (and_1_out, X, Y);
  and and_2 (and_2_out, C_i, Y);
  and and_3 (and_3_out, C_i, X);
  and and_4 (and_4_out, not_1_out, not_2_out, Y);
  and and_5 (and_5_out, not_1_out, X, not_3_out);
  and and_6 (and_6_out, C_i, not_2_out, not_3_out);
  and and_7 (and_7_out, C_i, X, Y);
  or or_1 (C_o, and_1_out, and_2_out, and_3_out);
  or or_2 (S, and_4_out, and_5_out, and_6_out, and_7_out);
endmodule

module HA (
  input  X,
  input  Y,
  output C_o,
  output S
);

  wire and_2_out, and_3_out, not_1_out, not_2_out;

  not not_1 (not_1_out, X);
  not not_2 (not_2_out, Y);
  and and_1 (C_o, X, Y);
  and and_2 (and_2_out, not_1_out, Y);
  and and_3 (and_3_out, X, not_2_out);
  or or_1 (S, and_2_out, and_3_out);
endmodule

module Circuit_Test (
  input  in_1,
  input  in_2,
  input  in_3,
  output out_4,
  output out_5,
  output out_6,
  output out_7
);

  HA ha_1 (.X(in_1), .Y(in_2), .C_o(out_4), .S(out_5));
  FA fa_1 (.X(in_3), .Y(in_1), .C_i(in_2), .C_o(out_6), .S(out_7));
endmodule

module RC (
  input  [3:0] X,
  input  [3:0] Y,
  output [3:0] z,
  output cout
);

  wire fa_1_c_o, fa_2_c_o, fa_3_c_o;

  FA fa_1 (.X(X[0]), .Y(Y[0]), .C_i(1'b0), .C_o(fa_1_c_o), .S(z[0]));
  FA fa_2 (.X(X[1]), .Y(Y[1]), .C_i(fa_1_c_o), .C_o(fa_2_c_o), .S(z[1]));
  FA fa_3 (.X(X[2]), .Y(Y[2]), .C_i(fa_2_c_o), .C_o(fa_3_c_o), .S(z[2]));
  FA fa_4 (.X(X[3]), .Y(Y[3]), .C_i(fa_3_c_o), .C_o(cout), .S(z[3]));

  // Other names for the same wires on the sheet: X_0 = X[0]; X_1 = X[1]; X_2 = X[2]; X_3 = X[3]; Y_0 = Y[0];
  //   Y_1 = Y[1]; Y_2 = Y[2]; Y_3 = Y[3]; Z_0 = z[0]; Z_1 = z[1]; Z_2 = z[2]; Z_3 = z[3]
endmodule

module RC_Select (
  input  A_S,
  input  [3:0] X,
  input  [3:0] Y,
  output [3:0] z,
  output cout
);

  wire fa_1_c_o, fa_2_c_o, fa_3_c_o, xor_1_out, xor_2_out, xor_3_out, xor_4_out;

  xor xor_1 (xor_1_out, A_S, Y[0]);
  xor xor_2 (xor_2_out, A_S, Y[1]);
  xor xor_3 (xor_3_out, A_S, Y[2]);
  xor xor_4 (xor_4_out, A_S, Y[3]);
  FA fa_1 (.X(X[0]), .Y(xor_1_out), .C_i(A_S), .C_o(fa_1_c_o), .S(z[0]));
  FA fa_2 (.X(X[1]), .Y(xor_2_out), .C_i(fa_1_c_o), .C_o(fa_2_c_o), .S(z[1]));
  FA fa_3 (.X(X[2]), .Y(xor_3_out), .C_i(fa_2_c_o), .C_o(fa_3_c_o), .S(z[2]));
  FA fa_4 (.X(X[3]), .Y(xor_4_out), .C_i(fa_3_c_o), .C_o(cout), .S(z[3]));

  // Other names for the same wires on the sheet: X_0 = X[0]; X_1 = X[1]; X_2 = X[2]; X_3 = X[3]; Y_0 = Y[0];
  //   Y_1 = Y[1]; Y_2 = Y[2]; Y_3 = Y[3]; Z_0 = z[0]; Z_1 = z[1]; Z_2 = z[2]; Z_3 = z[3]
endmodule

module BCD (
  input  A_S,
  input  [3:0] x0,
  input  [3:0] x1,
  input  [3:0] y1,
  input  [3:0] y0,
  input  in_6,
  input  in_7,
  input  in_8,
  output out_9,
  output [3:0] z_f1,
  output [3:0] z_f0,
  output [3:0] z1,
  output out_13,
  output [3:0] z0,
  output out_15,
  output [3:0] o,
  output out_17
);

  wire sev_seg_1_a, sev_seg_1_b, sev_seg_1_c, sev_seg_1_d, sev_seg_1_e, sev_seg_1_f, sev_seg_1_g,
       sev_seg_2_a, sev_seg_2_b, sev_seg_2_c, sev_seg_2_d, sev_seg_2_e, sev_seg_2_f, sev_seg_2_g,
       sev_seg_3_a, sev_seg_3_b, sev_seg_3_c, sev_seg_3_d, sev_seg_3_e, sev_seg_3_f, sev_seg_3_g,
       sev_seg_4_a, sev_seg_4_b, sev_seg_4_c, sev_seg_4_d, sev_seg_4_e, sev_seg_4_f, sev_seg_4_g,
       sev_seg_5_a, sev_seg_5_b, sev_seg_5_c, sev_seg_5_d, sev_seg_5_e, sev_seg_5_f, sev_seg_5_g,
       sev_seg_6_a, sev_seg_6_b, sev_seg_6_c, sev_seg_6_d, sev_seg_6_e, sev_seg_6_f, sev_seg_6_g;
  wire [3:0] overflow_1_z_out;

  sev_seg sev_seg_1 (
    .B_in(x1), .g(sev_seg_1_g), .f(sev_seg_1_f), .a(sev_seg_1_a), .b(sev_seg_1_b), .c(sev_seg_1_c),
    .e(sev_seg_1_e), .d(sev_seg_1_d));
  _7_Segment_Display u_7_segment_display_1 (
    .g(sev_seg_1_g), .f(sev_seg_1_f), .a(sev_seg_1_a), .b(sev_seg_1_b), .e(sev_seg_1_e), .d(sev_seg_1_d),
    .c(sev_seg_1_c));  // open: dp
  _7_Segment_Display u_7_segment_display_2 (
    .g(sev_seg_2_g), .f(sev_seg_2_f), .a(sev_seg_2_a), .b(sev_seg_2_b), .e(sev_seg_2_e), .d(sev_seg_2_d),
    .c(sev_seg_2_c));  // open: dp
  sev_seg sev_seg_2 (
    .B_in(x0), .g(sev_seg_2_g), .f(sev_seg_2_f), .a(sev_seg_2_a), .b(sev_seg_2_b), .c(sev_seg_2_c),
    .e(sev_seg_2_e), .d(sev_seg_2_d));
  RC_Select rc_select_1 (.A_S(A_S), .X(x1), .Y(y1), .z(z1), .cout(out_13));
  RC_Select rc_select_2 (.A_S(A_S), .X(x0), .Y(y0), .z(z0), .cout(out_17));
  sev_seg sev_seg_3 (
    .B_in(z_f1), .g(sev_seg_3_g), .f(sev_seg_3_f), .a(sev_seg_3_a), .b(sev_seg_3_b), .c(sev_seg_3_c),
    .e(sev_seg_3_e), .d(sev_seg_3_d));
  _7_Segment_Display u_7_segment_display_3 (.b(out_9), .c(out_9));  // open: g, f, a, e, d, dp
  sev_seg sev_seg_4 (
    .B_in(y1), .g(sev_seg_4_g), .f(sev_seg_4_f), .a(sev_seg_4_a), .b(sev_seg_4_b), .c(sev_seg_4_c),
    .e(sev_seg_4_e), .d(sev_seg_4_d));
  _7_Segment_Display u_7_segment_display_4 (
    .g(sev_seg_3_g), .f(sev_seg_3_f), .a(sev_seg_3_a), .b(sev_seg_3_b), .e(sev_seg_3_e), .d(sev_seg_3_d),
    .c(sev_seg_3_c));  // open: dp
  _7_Segment_Display u_7_segment_display_5 (
    .g(sev_seg_6_g), .f(sev_seg_6_f), .a(sev_seg_6_a), .b(sev_seg_6_b), .e(sev_seg_6_e), .d(sev_seg_6_d),
    .c(sev_seg_6_c));  // open: dp
  _7_Segment_Display u_7_segment_display_6 (
    .g(sev_seg_5_g), .f(sev_seg_5_f), .a(sev_seg_5_a), .b(sev_seg_5_b), .e(sev_seg_5_e), .d(sev_seg_5_d),
    .c(sev_seg_5_c));  // open: dp
  _7_Segment_Display u_7_segment_display_7 (
    .g(sev_seg_4_g), .f(sev_seg_4_f), .a(sev_seg_4_a), .b(sev_seg_4_b), .e(sev_seg_4_e), .d(sev_seg_4_d),
    .c(sev_seg_4_c));  // open: dp
  overflow overflow_1 (.z_in(z1), .c_out(out_9), .z_out(overflow_1_z_out));
  overflow overflow_2 (.z_in(z0), .c_out(o[0]), .z_out(z_f0));
  sev_seg sev_seg_5 (
    .B_in(y0), .g(sev_seg_5_g), .f(sev_seg_5_f), .a(sev_seg_5_a), .b(sev_seg_5_b), .c(sev_seg_5_c),
    .e(sev_seg_5_e), .d(sev_seg_5_d));
  sev_seg sev_seg_6 (
    .B_in(z_f0), .g(sev_seg_6_g), .f(sev_seg_6_f), .a(sev_seg_6_a), .b(sev_seg_6_b), .c(sev_seg_6_c),
    .e(sev_seg_6_e), .d(sev_seg_6_d));
  RC rc_1 (.X(overflow_1_z_out), .Y({in_8, in_7, in_6, o[0]}), .z(z_f1), .cout(out_15));

  assign o[3:1] = {in_8, in_7, in_6};

  // Notes on the sheet:
  //   +
  //   Result
endmodule

module overflow (
  input  [3:0] z_in,
  output c_out,
  output [3:0] z_out
);

  wire and_1_out, and_2_out, and_4_out, and_5_out, and_6_out, and_7_out, not_1_out, not_2_out, not_3_out;

  not not_1 (not_1_out, z_in[3]);
  not not_2 (not_2_out, z_in[2]);
  not not_3 (not_3_out, z_in[1]);
  and and_1 (and_1_out, z_in[3], z_in[1]);
  and and_2 (and_2_out, z_in[3], z_in[2]);
  and and_3 (z_out[3], z_in[3], not_2_out, not_3_out);
  and and_4 (and_4_out, not_1_out, z_in[2]);
  and and_5 (and_5_out, z_in[2], z_in[1]);
  and and_6 (and_6_out, not_1_out, z_in[1]);
  and and_7 (and_7_out, z_in[3], z_in[2], not_3_out);
  or or_1 (c_out, and_1_out, and_2_out);
  or or_2 (z_out[2], and_4_out, and_5_out);
  or or_3 (z_out[1], and_6_out, and_7_out);

  assign z_out[0] = z_in[0];
endmodule

module BCD_S (
  input  [3:0] x1,
  input  [3:0] x0,
  input  [3:0] y0,
  input  [3:0] y1,
  output out_5,
  output [3:0] out_6,
  output [3:0] z_0,
  output out_8,
  output out_9,
  output [3:0] out_10
);

  wire [3:0] overflow_1_z_out, rc_select_1_z, rc_select_2_z;

  RC_Select rc_select_1 (.A_S(1'b0), .X(x1), .Y(y1), .z(rc_select_1_z), .cout(out_8));
  RC_Select rc_select_2 (.A_S(1'b0), .X(x0), .Y(y0), .z(rc_select_2_z), .cout(out_9));
  overflow overflow_1 (.z_in(rc_select_1_z), .c_out(out_5), .z_out(overflow_1_z_out));
  overflow overflow_2 (.z_in(rc_select_2_z), .c_out(out_10[0]), .z_out(z_0));
  RC rc_1 (.X(overflow_1_z_out), .Y({3'b000, out_10[0]}), .z(out_6));  // open: cout

  assign out_10[3:1] = 3'b000;

  // Notes on the sheet:
  //   MSBs
  //   LSBs
endmodule

module sev_seg (
  input  [3:0] B_in,
  output g,
  output f,
  output a,
  output b,
  output c,
  output e,
  output d
);

  wire and_1_out, and_2_out, and_3_out, and_4_out, and_5_out, and_6_out, and_7_out, and_8_out, and_9_out,
       and_10_out, and_11_out, and_12_out, and_13_out, and_14_out, and_15_out, and_16_out, and_17_out,
       and_18_out, and_19_out, and_20_out, and_21_out, and_22_out, and_23_out, not_1_out, not_2_out,
       not_3_out, not_4_out;

  not not_1 (not_1_out, B_in[3]);
  not not_2 (not_2_out, B_in[2]);
  not not_3 (not_3_out, B_in[1]);
  not not_4 (not_4_out, B_in[0]);
  and and_1 (and_1_out, not_2_out, B_in[1]);
  and and_2 (and_2_out, B_in[2], not_3_out);
  and and_3 (and_3_out, B_in[1], not_4_out);
  and and_4 (and_4_out, not_3_out, not_4_out);
  and and_5 (and_5_out, B_in[2], not_3_out);
  and and_6 (and_6_out, B_in[2], not_4_out);
  and and_7 (and_7_out, not_2_out, not_4_out);
  and and_8 (and_8_out, B_in[2], B_in[0]);
  and and_9 (and_9_out, not_1_out, not_2_out);
  and and_10 (and_10_out, not_1_out, not_3_out, not_4_out);
  and and_11 (and_11_out, not_1_out, B_in[1], B_in[0]);
  and and_12 (and_12_out, not_2_out, not_3_out);
  and and_13 (and_13_out, not_1_out, B_in[0]);
  and and_14 (and_14_out, not_1_out, B_in[2]);
  and and_15 (and_15_out, not_2_out, not_3_out);
  and and_16 (and_16_out, not_2_out, not_4_out);
  and and_17 (and_17_out, B_in[1], not_4_out);
  and and_18 (and_18_out, B_in[3], B_in[1]);
  and and_19 (and_19_out, B_in[3], B_in[2]);
  and and_20 (and_20_out, not_2_out, not_4_out);
  and and_21 (and_21_out, not_2_out, B_in[1]);
  and and_22 (and_22_out, B_in[2], not_3_out, B_in[0]);
  and and_23 (and_23_out, B_in[1], not_4_out);
  or or_1 (g, and_1_out, and_2_out, B_in[3], and_3_out);
  or or_2 (f, and_4_out, and_5_out, and_6_out, B_in[3]);
  or or_3 (a, and_7_out, B_in[1], and_8_out, B_in[3]);
  or or_4 (b, and_9_out, and_10_out, and_11_out, and_12_out);
  or or_5 (c, and_13_out, and_14_out, and_15_out);
  or or_6 (e, and_16_out, and_17_out, and_18_out, and_19_out);
  or or_7 (d, and_20_out, and_21_out, and_22_out, and_23_out, B_in[3]);
endmodule
