// Logisim project Latches_and_FF.circ as structural Verilog
module SR_latch (
  input  R,
  input  S,
  output Q,
  output Qnot
);

  nor nor_1 (Q, R, Qnot);
  nor nor_2 (Qnot, Q, S);
endmodule

module Gated_SR (
  input  R,
  input  E,
  input  S,
  output Q,
  output Qnot
);

  wire and_1_out, and_2_out;

  and and_1 (and_1_out, R, E);
  and and_2 (and_2_out, E, S);
  nor nor_1 (Q, and_1_out, Qnot);
  nor nor_2 (Qnot, Q, and_2_out);
endmodule

module D_latch (
  input  E,
  input  D,
  output Q,
  output Qnot
);

  wire and_1_out, and_2_out, not_1_out;

  not not_1 (not_1_out, D);
  and and_1 (and_1_out, not_1_out, E);
  and and_2 (and_2_out, E, D);
  nor nor_1 (Q, and_1_out, Qnot);
  nor nor_2 (Qnot, Q, and_2_out);
endmodule

module D_flipFlop (
  input  D,
  output Q,
  output Qnot
);

  wire and_1_out, and_2_out, Clk_out, not_1_out;

  Clock Clk (.out(Clk_out));
  not not_1 (not_1_out, D);
  and and_1 (and_1_out, not_1_out, Clk_out);
  and and_2 (and_2_out, Clk_out, D);
  nor nor_1 (Q, and_1_out, Qnot);
  nor nor_2 (Qnot, Q, and_2_out);
endmodule
