// Logisim project Matrix_Keypad.circ as structural Verilog
module membrane (
  input  [2:0] in_1,
  input  [1:0] in_2,
  input  [2:0] in_3,
  input  [2:0] in_4,
  output [2:0] Cols,
  output [1:0] out_6,
  output [2:0] Rows
);

  wire clock_1_out, comparator_1_eq;

  Clock clock_1 (.out(clock_1_out));
  Counter #(.max('h3), .width(2)) counter_1 (
    .Q(out_6), .clk(clock_1_out), .clr(comparator_1_eq));  // open: load, D, count, carry, up
  Comparator #(.width(2)) comparator_1 (.a(out_6), .b(in_2), .eq(comparator_1_eq));  // open: gt, lt
  Pull_Resistor #(.pull(1)) pull_resistor_1 (.node(Cols[0]));
  // Switch switch_1: pin names not known; wires that end beside it: Rows[0], Cols[0]
  // Switch switch_2: pin names not known; wires that end beside it: Rows[1], Cols[0]
  // Switch switch_3: pin names not known; wires that end beside it: Rows[2], Cols[0]
  Pull_Resistor #(.pull(1)) pull_resistor_2 (.node(Cols[1]));
  // Switch switch_4: pin names not known; wires that end beside it: Rows[0], Cols[1]
  // Switch switch_5: pin names not known; wires that end beside it: Rows[1], Cols[1]
  // Switch switch_6: pin names not known; wires that end beside it: Rows[2], Cols[1]
  Pull_Resistor #(.pull(1)) pull_resistor_3 (.node(Cols[2]));
  // Switch switch_7: pin names not known; wires that end beside it: Rows[0], Cols[2]
  // Switch switch_8: pin names not known; wires that end beside it: Rows[1], Cols[2]
  // Switch switch_9: pin names not known; wires that end beside it: Rows[2], Cols[2]
  Multiplexer #(.select(2), .width(3)) multiplexer_1 (
    .in0(in_1), .in1(in_3), .in2(in_4), .out(Rows), .sel(out_6));  // open: in3
endmodule
