// Logisim project adder_circ.circ as structural Verilog: 2 circuits, main circuit main
module main (
  input  A,
  input  B,
  input  C,
  output Sum,
  output Cout
);

  wire ha_1_c_out, ha_1_o, ha_2_c_out;

  HA ha_1 (.x(A), .y(B), .O(ha_1_o), .C_out(ha_1_c_out));
  HA ha_2 (.x(ha_1_o), .y(C), .O(Sum), .C_out(ha_2_c_out));
  or or_1 (Cout, ha_2_c_out, ha_1_c_out);
endmodule

module HA (
  input  x,
  input  y,
  output O,
  output C_out
);

  and and_1 (C_out, x, y);
  xor xor_1 (O, x, y);
endmodule
