// Logisim project Adders_with_MUX.circ as structural Verilog: 3 circuits, main circuit main
module main (
  input  C_on,
  input  A,
  input  B,
  input  S,
  output C_out,
  output Sum,
  output Mode
);

  wire C_out_0, C_out_1, Sum_0, Sum_1;

  Full_adder_mux Full_adder_mux_1 (.C_in(C_on), .A(A), .B(B), .C_out(C_out_0), .Sum(Sum_0));
  Decoder_FA decoder_fa_1 (.C_in(C_on), .A(A), .B(B), .C_out(C_out_1), .Sum(Sum_1));
  Multiplexer multiplexer_1 (.in0(C_out_0), .in1(C_out_1), .out(C_out), .sel(S));
  Multiplexer multiplexer_2 (.in0(Sum_0), .in1(Sum_1), .out(Sum), .sel(S));

  assign Mode = S;
endmodule

module Full_adder_mux (
  input  C_in,
  input  A,
  input  B,
  output C_out,
  output Sum
);

  Multiplexer #(.select(3)) multiplexer_1 (
    .in0(1'b0), .in1(1'b0), .in2(1'b0), .in3(1'b1), .in4(1'b0), .in5(1'b1), .in6(1'b1), .in7(1'b1),
    .out(C_out), .sel({B, A, C_in}));
  Multiplexer #(.select(3)) multiplexer_2 (
    .in0(1'b0), .in1(1'b1), .in2(1'b1), .in3(1'b0), .in4(1'b1), .in5(1'b0), .in6(1'b0), .in7(1'b1),
    .out(Sum), .sel({B, A, C_in}));
endmodule

module Decoder_FA (
  input  C_in,
  input  A,
  input  B,
  output C_out,
  output Sum
);

  wire decoder_1_out3, decoder_1_out5, decoder_1_out6, decoder_1_out7, decoder_2_out1, decoder_2_out2,
       decoder_2_out4, decoder_2_out7;

  Decoder #(.select(3)) decoder_1 (
    .out3(decoder_1_out3), .out5(decoder_1_out5), .out6(decoder_1_out6), .out7(decoder_1_out7),
    .sel({B, A, C_in}));  // open: out0, out1, out2, out4, en
  or or_1 (C_out, decoder_1_out3, decoder_1_out5, decoder_1_out6, decoder_1_out7);
  Decoder #(.select(3)) decoder_2 (
    .out1(decoder_2_out1), .out2(decoder_2_out2), .out4(decoder_2_out4), .out7(decoder_2_out7),
    .sel({B, A, C_in}));  // open: out0, out3, out5, out6, en
  or or_2 (Sum, decoder_2_out1, decoder_2_out2, decoder_2_out4, decoder_2_out7);
endmodule
