// Logisim project neg_7seg.circ as structural Verilog: 1 circuit, main circuit main
module main (
  input  B3,
  input  B2,
  input  B1,
  input  B0,
  output g1,
  output a,
  output b,
  output c,
  output d,
  output e,
  output f,
  output g2
);

  wire and_1_out, and_2_out, and_3_out, and_4_out, and_5_out, and_6_out, and_7_out, and_8_out, and_9_out,
       and_10_out, and_11_out, and_12_out, and_13_out, and_14_out, and_15_out, and_16_out, and_17_out,
       and_18_out, and_19_out, and_20_out, and_21_out, and_22_out, and_23_out, and_24_out, and_25_out,
       and_26_out, not_1_out, not_2_out, not_3_out, not_4_out;

  not not_1 (not_1_out, B3);
  not not_2 (not_2_out, B2);
  not not_3 (not_3_out, B1);
  not not_4 (not_4_out, B0);
  and and_1 (and_1_out, not_2_out, not_4_out);
  and and_2 (and_2_out, B1, not_4_out);
  and and_3 (and_3_out, not_1_out, B1);
  and and_4 (and_4_out, B3, not_2_out);
  and and_5 (and_5_out, B2, not_3_out, B0);
  and and_6 (and_6_out, not_1_out, not_2_out);
  and and_7 (and_7_out, not_3_out, not_4_out);
  and and_8 (and_8_out, B3, B2);
  and and_9 (and_9_out, not_1_out, B1, B0);
  and and_10 (and_10_out, B3, not_3_out);
  and and_11 (and_11_out, not_1_out, B2);
  and and_12 (and_12_out, B3, not_2_out);
  and and_13 (and_13_out, B1, not_4_out);
  and and_14 (and_14_out, not_2_out, not_4_out);
  and and_15 (and_15_out, not_2_out, B1);
  and and_16 (and_16_out, B2, not_3_out, B0);
  and and_17 (and_17_out, not_2_out, not_4_out);
  and and_18 (and_18_out, B1, not_4_out);
  and and_19 (and_19_out, not_3_out, not_4_out);
  and and_20 (and_20_out, not_1_out, B2, not_3_out);
  and and_21 (and_21_out, not_1_out, B2, not_4_out);
  and and_22 (and_22_out, B3, not_2_out, B1);
  and and_23 (and_23_out, not_2_out, B1);
  and and_24 (and_24_out, B2, not_3_out);
  and and_25 (and_25_out, B3, not_4_out);
  and and_26 (and_26_out, B1, not_4_out);
  or or_1 (a, and_1_out, and_2_out, and_3_out, and_4_out, and_5_out);
  or or_2 (b, and_6_out, and_7_out, and_8_out, and_9_out, and_10_out);
  or or_3 (c, not_3_out, B0, and_11_out, and_12_out);
  or or_4 (d, and_13_out, and_14_out, and_15_out, and_16_out);
  or or_5 (e, and_17_out, and_18_out);
  or or_6 (f, and_19_out, and_20_out, and_21_out, and_22_out);
  or or_7 (g2, and_23_out, and_24_out, and_25_out, and_26_out);
  _7_Segment_Display u_7_segment_display_1 (.g(B3));  // open: f, a, b, e, d, c, dp
  _7_Segment_Display u_7_segment_display_2 (.g(g2), .f(f), .a(a), .b(b), .e(e), .d(d), .c(c));  // open: dp

  assign g1 = B3;
endmodule
