// Logisim project shift_regs.circ as structural Verilog: 2 circuits, main circuit main
module main (
  input  serial_in,
  input  clk,
  output [3:0] serial_out
);

  D_Flip_Flop d_ff_1 (.D(serial_in), .clk(clk), .Q(serial_out[3]));  // open: Qn, preset, reset
  D_Flip_Flop d_ff_2 (.D(serial_out[3]), .clk(clk), .Q(serial_out[2]));  // open: Qn, preset, reset
  D_Flip_Flop d_ff_3 (.D(serial_out[2]), .clk(clk), .Q(serial_out[1]));  // open: Qn, preset, reset
  D_Flip_Flop d_ff_4 (.D(serial_out[1]), .clk(clk), .Q(serial_out[0]));  // open: Qn, preset, reset
endmodule

module para_acc_shift (
  input  load,
  input  serial_in,
  input  clk,
  input  [3:0] para_input,
  output [3:0] Q
);

  wire multiplexer_1_out, multiplexer_2_out, multiplexer_3_out, multiplexer_4_out;

  Multiplexer multiplexer_1 (.in0(serial_in), .in1(para_input[3]), .out(multiplexer_1_out), .sel(load));
  D_Flip_Flop d_ff_1 (.D(multiplexer_1_out), .clk(clk), .Q(Q[3]));  // open: Qn, preset, reset
  D_Flip_Flop d_ff_2 (.D(multiplexer_2_out), .clk(clk), .Q(Q[2]));  // open: Qn, preset, reset
  Multiplexer multiplexer_2 (.in0(Q[3]), .in1(para_input[2]), .out(multiplexer_2_out), .sel(load));
  D_Flip_Flop d_ff_3 (.D(multiplexer_3_out), .clk(clk), .Q(Q[1]));  // open: Qn, preset, reset
  Multiplexer multiplexer_3 (.in0(Q[2]), .in1(para_input[1]), .out(multiplexer_3_out), .sel(load));
  D_Flip_Flop d_ff_4 (.D(multiplexer_4_out), .clk(clk), .Q(Q[0]));  // open: Qn, preset, reset
  Multiplexer multiplexer_4 (.in0(Q[1]), .in1(para_input[0]), .out(multiplexer_4_out), .sel(load));
endmodule
