// Logisim project HW5.circ as structural Verilog
module Q1 (
  input  [2:0] ABC,
  output f
);

  wire decoder_1_out1, decoder_1_out2, decoder_1_out3, decoder_1_out5, decoder_1_out6;

  Decoder #(.select(3)) decoder_1 (
    .out1(decoder_1_out1), .out2(decoder_1_out2), .out3(decoder_1_out3), .out5(decoder_1_out5),
    .out6(decoder_1_out6), .sel(ABC));  // open: out0, out4, out7, en
  or or_1 (f, decoder_1_out1, decoder_1_out2, decoder_1_out3, decoder_1_out5, decoder_1_out6);
endmodule

module Q2 (
  input  B,
  input  C,
  input  s,
  output f
);

  wire and_1_out, or_1_out;

  or or_1 (or_1_out, B, ~C);  // OR_Gate
  and and_1 (and_1_out, B, ~C);  // AND_Gate
  Multiplexer multiplexer_1 (.in0(or_1_out), .in1(and_1_out), .out(f), .sel(s));
endmodule

module Q3 (
  input  B,
  input  C,
  input  A,
  output out_4
);

  wire nor_1_out, or_1_out;

  nor nor_1 (nor_1_out, B, C);
  or or_1 (or_1_out, B, ~C);  // OR_Gate
  Multiplexer multiplexer_1 (.in0(nor_1_out), .in1(or_1_out), .out(out_4), .sel(A));
endmodule

module Q4 (
  input  B,
  input  C,
  input  A,
  output f
);

  wire and_1_out, or_1_out;

  or or_1 (or_1_out, B, ~C);  // OR_Gate
  and and_1 (and_1_out, B, ~C);  // AND_Gate
  Multiplexer multiplexer_1 (.in0(or_1_out), .in1(and_1_out), .out(f), .sel(A));
endmodule

module Q5 (
  input  C,
  input  A,
  input  B,
  output f
);

  wire not_1_out;

  not not_1 (not_1_out, C);
  Multiplexer #(.select(2)) multiplexer_1 (.in0(1'b1), .in1(1'b0), .in2(not_1_out), .in3(C), .out(f), .sel({A, B}));
endmodule

module Q5_2 (
  input  B,
  input  C,
  input  A,
  output f
);

  wire multiplexer_1_out, not_1_out, not_2_out;

  not not_1 (not_1_out, C);
  not not_2 (not_2_out, B);
  Multiplexer multiplexer_1 (.in0(not_1_out), .in1(C), .out(multiplexer_1_out), .sel(B));
  Multiplexer multiplexer_2 (.in0(not_2_out), .in1(multiplexer_1_out), .out(f), .sel(A));
endmodule
