// Logisim project Lab_05.circ as structural Verilog: 2 circuits, main circuit main
module main (
  input  Input_1,
  input  Input_2,
  output Output_1,
  output Output_2
);


  assign Output_1 = Input_1;
  assign Output_2 = Input_2;
endmodule

module full_adder (
  input  A,
  input  B,
  input  C,
  output Sum,
  output C_out
);

  wire and_1_out, and_2_out, and_3_out, and_4_out, and_5_out, and_6_out, and_7_out, not_1_out, not_2_out,
       not_3_out;

  not not_1 (not_1_out, A);
  not not_2 (not_2_out, B);
  not not_3 (not_3_out, C);
  and and_1 (and_1_out, not_1_out, not_2_out, C);
  and and_2 (and_2_out, not_1_out, B, not_3_out);
  and and_3 (and_3_out, A, not_2_out, not_3_out);
  and and_4 (and_4_out, A, B, C);
  and and_5 (and_5_out, B, C);
  and and_6 (and_6_out, A, C);
  or or_1 (C_out, and_5_out, and_6_out, and_7_out);
  and and_7 (and_7_out, A, B);
  or or_2 (Sum, and_1_out, and_2_out, and_3_out, and_4_out);
endmodule
