// Logisim project Lab_08_Circ.circ as structural Verilog
module main (
  input  [1:0] sel,
  input  en,
  output B,
  output G,
  output R
);

  wire clk_out;
  wire [0:0] comparator_1_eq;
  wire [1:0] counter_1_q;
  wire [2:0] LED_FSM_1_state;
  wire [2:2] and_1_out;

  Clock clk (.out(clk_out));
  and and_1 (and_1_out[2], clk_out, en);
  Counter #(.max('h3), .width(2)) counter_1 (
    .load(comparator_1_eq[0]), .D(2'b10), .Q(counter_1_q), .up(1'b0), .clk(and_1_out[2]));  // open: count, carry, clr
  LED_FSM LED_FSM_1 (.NextState(and_1_out[2]), .State(LED_FSM_1_state));
  Comparator #(.width(2)) comparator_1 (.a(counter_1_q), .b(2'b00), .eq(comparator_1_eq[0]));  // open: gt, lt
  Multiplexer #(.select(2), .width(3)) multiplexer_1 (
    .in0(LED_FSM_1_state), .in1({and_1_out[2], 2'b00}), .in2({2'b00, comparator_1_eq[0]}),
    .in3({1'b0, en, 1'b0}), .out({R, G, B}), .sel(sel));

  // Notes on the sheet:
  //   Blink Red
  //   Blink Blue (Slower)
  //   Hold Green
endmodule

module LED_FSM (
  input  NextState,
  output [2:0] State
);

  wire [2:0] multiplexer_1_out;

  Multiplexer #(.select(3), .width(3)) multiplexer_1 (
    .in0(3'b001), .in1(3'b010), .in2(3'b011), .in3(3'b100), .in4(3'b101), .in5(3'b110), .in6(3'b111),
    .in7(3'b000), .out(multiplexer_1_out), .sel(State));
  // Probe on multiplexer_1_out
  Register #(.width(3)) register_1 (.D(multiplexer_1_out), .Q(State), .clk(NextState));  // open: en, clr
  // Probe on State
endmodule
