// Logisim project final_project.circ as structural Verilog: 12 circuits, main circuit main
module main (
  input  en
);

  wire and_1_out, and_2_out, clk, G, next_state, or_1_out, pedestrian_button_1_en, R, Y;
  wire [3:0] DownCounter3_1_count;
  wire [7:0] HEX0, HEX1;

  and and_1 (and_1_out, en, and_2_out);
  and and_2 (and_2_out, ~DownCounter3_1_count[0], ~DownCounter3_1_count[1], ~DownCounter3_1_count[2], ~DownCounter3_1_count[3]);  // AND_Gate
  Clock u_clk (.out(clk));
  or or_1 (or_1_out, next_state, pedestrian_button_1_en);
  // RGBLED REd: pin names not known; wires that end beside it: R
  // RGBLED yell: pin names not known; wires that end beside it: Y, Y
  // RGBLED gree: pin names not known; wires that end beside it: G
  FSM FSM_1 (.en(en), .next_state(and_1_out), .G(G), .Y(Y), .R(R), .rst(next_state));
  _7_Segment_Display #(.active("false")) L_7_Segment_Display_1 (
    .g(HEX1[6]), .f(HEX1[5]), .a(HEX1[0]), .b(HEX1[1]), .e(HEX1[4]), .d(HEX1[3]), .c(HEX1[2]), .dp(HEX1[7]));
  DownCounter3 DownCounter3_1 (.en(or_1_out), .clk(clk), .count(DownCounter3_1_count));
  pedestrian_button pedestrian_button_1 (.counter(DownCounter3_1_count), .en(pedestrian_button_1_en));
  _7_Segment_Display #(.active("false")) L_7_Segment_Display_2 (
    .g(HEX0[6]), .f(HEX0[5]), .a(HEX0[0]), .b(HEX0[1]), .e(HEX0[4]), .d(HEX0[3]), .c(HEX0[2]), .dp(HEX0[7]));
  Bin2Hex Bin2Hex_1 (
    .v3(DownCounter3_1_count[3]), .v2(DownCounter3_1_count[2]), .v1(DownCounter3_1_count[1]),
    .v0(DownCounter3_1_count[0]), .HEX1(HEX1), .HEX0(HEX0));

  // Notes on the sheet:
  //   Traffic Light A
  //   Counter Display
endmodule

module Seg7_Decoder (
  input  i_m3,
  input  i_m2,
  input  i_m1,
  input  i_m0,
  output [7:0] o_seg
);

  wire and_1_out, and_2_out, and_3_out, and_4_out, and_5_out, and_6_out, and_7_out, and_8_out, and_9_out,
       and_10_out, and_11_out, and_12_out, and_13_out, and_14_out, and_15_out, and_16_out, and_17_out,
       and_18_out, and_19_out, and_20_out, and_21_out, and_22_out, and_23_out, not_1_out, not_2_out,
       not_3_out, not_4_out;

  not not_1 (not_1_out, i_m3);
  not not_2 (not_2_out, i_m2);
  not not_3 (not_3_out, i_m1);
  not not_4 (not_4_out, i_m0);
  and and_1 (and_1_out, not_1_out, not_2_out, not_3_out);
  and and_2 (and_2_out, not_1_out, i_m2, i_m1, i_m0);
  and and_3 (and_3_out, i_m3, not_2_out, i_m1);
  and and_4 (and_4_out, not_1_out, not_2_out, i_m0);
  and and_5 (and_5_out, not_1_out, not_2_out, i_m1);
  and and_6 (and_6_out, not_2_out, i_m1, i_m0);
  and and_7 (and_7_out, i_m3, i_m2, not_3_out);
  and and_8 (and_8_out, not_1_out, i_m2, not_3_out);
  and and_9 (and_9_out, i_m3, i_m2, i_m1);
  and and_10 (and_10_out, not_1_out, not_2_out, not_3_out, i_m0);
  and and_11 (and_11_out, not_1_out, i_m2, not_3_out, not_4_out);
  and and_12 (and_12_out, not_1_out, i_m2, i_m1, i_m0);
  and and_13 (and_13_out, i_m3, not_2_out, i_m1, i_m0);
  and and_14 (and_14_out, i_m3, i_m2, i_m1, not_4_out);
  and and_15 (and_15_out, not_1_out, not_2_out, i_m1, not_4_out);
  and and_16 (and_16_out, i_m3, i_m2, not_3_out, not_4_out);
  and and_17 (and_17_out, not_1_out, i_m2, not_3_out, i_m0);
  and and_18 (and_18_out, not_1_out, i_m2, i_m1, not_4_out);
  and and_19 (and_19_out, i_m3, i_m2, i_m1, i_m0);
  and and_20 (and_20_out, not_1_out, not_2_out, not_3_out, i_m0);
  and and_21 (and_21_out, not_1_out, i_m2, not_3_out, not_4_out);
  and and_22 (and_22_out, i_m3, not_2_out, i_m1, i_m0);
  and and_23 (and_23_out, i_m3, i_m2, i_m1, not_4_out);
  or or_1 (o_seg[6], and_1_out, and_2_out, and_3_out);
  or or_2 (o_seg[5], and_4_out, and_5_out, and_6_out, and_7_out);
  or or_3 (o_seg[4], i_m0, and_8_out, and_9_out);
  or or_4 (o_seg[3], and_10_out, and_11_out, and_12_out, and_13_out, and_14_out);
  or or_5 (o_seg[2], and_15_out, and_16_out);
  or or_6 (o_seg[1], and_17_out, and_18_out, and_19_out);
  or or_7 (o_seg[0], and_20_out, and_21_out, and_22_out, and_23_out);

  assign o_seg[7] = 1'b1;
endmodule

module CircuitA (
  input  i2,
  input  i1,
  input  i0,
  output o2,
  output o1,
  output o0
);

  not not_1 (o1, i1);
  and and_1 (o2, i2, i1);

  assign o0 = i0;
endmodule

module myComparator (
  input  v3,
  input  v2,
  input  v1,
  input  v0,
  output z
);

  wire and_1_out, and_2_out;

  and and_1 (and_1_out, v3, v1);
  and and_2 (and_2_out, v3, v2);
  or or_1 (z, and_1_out, and_2_out);
endmodule

module CircuitB (
  input  z,
  output s6,
  output s5,
  output s4,
  output s3,
  output s2,
  output s1,
  output s0
);


  assign s0 = z;
  assign s1 = 1'b0;
  assign s2 = 1'b0;
  assign s3 = z;
  assign s4 = z;
  assign s5 = z;
  assign s6 = 1'b1;
endmodule

module Bin2Hex (
  input  v3,
  input  v2,
  input  v1,
  input  v0,
  output [7:0] HEX1,
  output [7:0] HEX0
);

  wire z;

  myComparator myComparator_1 (.v3(v3), .v2(v2), .v1(v1), .v0(v0), .z(z));
  CircuitB CircuitB_1 (
    .z(z), .s6(HEX1[6]), .s5(HEX1[5]), .s4(HEX1[4]), .s3(HEX1[3]), .s2(HEX1[2]), .s1(HEX1[1]), .s0(HEX1[0]));
  Seg7_Decoder Seg7_Decoder_1 (.i_m3(v3), .i_m2(v2), .i_m1(v1), .i_m0(v0), .o_seg(HEX0));

  assign HEX1[7] = 1'b1;
endmodule

module pedestrian_button (
  input  [3:0] counter,
  output en
);

  or or_1 (en, counter[0], counter[1], counter[2], counter[3]);
endmodule

module FSM (
  input  en,
  input  next_state,
  output G,
  output Y,
  output R,
  output rst
);

  wire [1:0] multiplexer_1_out, register_1_q;

  Multiplexer #(.select(3), .width(2)) multiplexer_1 (
    .in0(2'b00), .in1(2'b01), .in2(2'b10), .in4(2'b01), .in5(2'b10), .in6(2'b00), .out(multiplexer_1_out),
    .sel({en, register_1_q}));  // open: in3, in7
  // Probe on multiplexer_1_out
  Register #(.width(2)) register_1 (.D(multiplexer_1_out), .Q(register_1_q), .clk(next_state));  // open: en, clr
  // Probe on register_1_q
  and and_1 (G, ~register_1_q[0], ~register_1_q[1]);  // AND_Gate
  and and_2 (Y, register_1_q[0], ~register_1_q[1]);  // AND_Gate
  and and_3 (R, ~register_1_q[0], register_1_q[1]);  // AND_Gate

  assign rst = next_state;
endmodule

module DownCounter10 (
  input  en,
  input  clk,
  output [3:0] count
);

  wire and_1_out, and_2_out, and_3_out, and_4_out, t_ff_1_q, t_ff_2_q, t_ff_3_q;

  T_Flip_Flop t_ff_1 (.T(en), .clk(clk), .Q(t_ff_1_q), .Qn(count[0]), .preset(and_1_out));  // open: reset
  and and_1 (and_1_out, count[0], count[1], count[2], count[3]);
  and and_2 (and_2_out, en, t_ff_1_q);
  T_Flip_Flop t_ff_2 (.T(and_2_out), .clk(clk), .Q(t_ff_2_q), .Qn(count[1]));  // open: reset, preset
  and and_3 (and_3_out, and_2_out, t_ff_2_q);
  T_Flip_Flop t_ff_3 (.T(and_3_out), .clk(clk), .Q(t_ff_3_q), .Qn(count[2]), .preset(and_1_out));  // open: reset
  and and_4 (and_4_out, and_3_out, t_ff_3_q);
  T_Flip_Flop t_ff_4 (.T(and_4_out), .clk(clk), .Qn(count[3]));  // open: Q, reset, preset

  // Notes on the sheet:
  //   Synchronous Down Counter from 10 to 0 with reset
endmodule

module DownCounter3 (
  input  en,
  input  clk,
  output [3:0] count
);

  wire and_1_out, and_2_out, and_3_out, and_4_out, t_ff_1_q, t_ff_2_q, t_ff_3_q;

  T_Flip_Flop t_ff_1 (.T(en), .clk(clk), .Q(t_ff_1_q), .Qn(count[0]));  // open: reset, preset
  and and_1 (and_1_out, count[0], count[1], count[2], count[3]);
  and and_2 (and_2_out, en, t_ff_1_q);
  T_Flip_Flop t_ff_2 (.T(and_2_out), .clk(clk), .Q(t_ff_2_q), .Qn(count[1]));  // open: reset, preset
  and and_3 (and_3_out, and_2_out, t_ff_2_q);
  T_Flip_Flop t_ff_3 (.T(and_3_out), .clk(clk), .Q(t_ff_3_q), .Qn(count[2]), .preset(and_1_out));  // open: reset
  and and_4 (and_4_out, and_3_out, t_ff_3_q);
  T_Flip_Flop t_ff_4 (.T(and_4_out), .clk(clk), .Qn(count[3]), .preset(and_1_out));  // open: Q, reset

  // Notes on the sheet:
  //   Synchronous Down Counter from 3 to 0 with reset
endmodule

module FSM_TwoLights (
  input  en,
  input  NextState,
  output RG,
  output RY,
  output GR,
  output YR
);

  wire [1:0] multiplexer_1_out, register_1_q;

  Multiplexer #(.select(3), .width(2)) multiplexer_1 (
    .in0(2'b00), .in1(2'b01), .in2(2'b10), .in3(2'b11), .in4(2'b01), .in5(2'b10), .in6(2'b11), .in7(2'b00),
    .out(multiplexer_1_out), .sel({en, register_1_q}));
  // Probe on multiplexer_1_out
  Register #(.width(2)) register_1 (.D(multiplexer_1_out), .Q(register_1_q), .clk(NextState));  // open: en, clr
  // Probe on register_1_q
  and and_1 (RG, ~register_1_q[1], ~register_1_q[0]);  // AND_Gate
  and and_2 (RY, ~register_1_q[1], register_1_q[0]);  // AND_Gate
  and and_3 (GR, register_1_q[1], ~register_1_q[0]);  // AND_Gate
  and and_4 (YR, register_1_q[1], register_1_q[0]);
endmodule

module FSM_ped (
  input  PED_button,
  input  NextState,
  output RG,
  output RY,
  output GR,
  output YR,
  output RR
);

  wire [2:0] multiplexer_1_out, register_1_q;

  // Probe on multiplexer_1_out
  Multiplexer #(.select(4), .width(3)) multiplexer_1 (
    .in0(3'b000), .in1(3'b001), .in2(3'b010), .in3(3'b011), .in4(3'b001), .in5(3'b010), .in6(3'b011),
    .in7(3'b000), .in8(3'b100), .in9(3'b100), .in10(3'b100), .in11(3'b100), .in12(3'b100), .in13(3'b100),
    .in14(3'b100), .in15(3'b100), .out(multiplexer_1_out), .sel({PED_button, register_1_q}));
  Register #(.width(3)) register_1 (.D(multiplexer_1_out), .Q(register_1_q), .clk(NextState));  // open: en, clr
  // Probe on register_1_q
  and and_1 (RG, ~register_1_q[2], ~register_1_q[1], ~register_1_q[0]);  // AND_Gate
  and and_2 (RY, ~register_1_q[2], ~register_1_q[1], register_1_q[0]);  // AND_Gate
endmodule
