// Logisim project 4Bit_ALU_ASAO.circ as structural Verilog: 6 circuits, main circuit main
module main (
  input  [3:0] A,
  input  [3:0] B,
  input  [1:0] Oper_S,
  output Neg_LED
);

  wire sev_seg_hex_decoder_1_a, sev_seg_hex_decoder_1_b, sev_seg_hex_decoder_1_c, sev_seg_hex_decoder_1_d,
       sev_seg_hex_decoder_1_dec, sev_seg_hex_decoder_1_e, sev_seg_hex_decoder_1_f, sev_seg_hex_decoder_1_g,
       sev_seg_hex_decoder_2_a, sev_seg_hex_decoder_2_b, sev_seg_hex_decoder_2_c, sev_seg_hex_decoder_2_d,
       sev_seg_hex_decoder_2_dec, sev_seg_hex_decoder_2_e, sev_seg_hex_decoder_2_f, sev_seg_hex_decoder_2_g,
       sev_seg_hex_decoder_3_a, sev_seg_hex_decoder_3_b, sev_seg_hex_decoder_3_c, sev_seg_hex_decoder_3_d,
       sev_seg_hex_decoder_3_dec, sev_seg_hex_decoder_3_e, sev_seg_hex_decoder_3_f, sev_seg_hex_decoder_3_g,
       sev_seg_hex_decoder_4_a, sev_seg_hex_decoder_4_b, sev_seg_hex_decoder_4_c, sev_seg_hex_decoder_4_d,
       sev_seg_hex_decoder_4_dec, sev_seg_hex_decoder_4_e, sev_seg_hex_decoder_4_f, sev_seg_hex_decoder_4_g,
       SUB;
  wire [3:0] Carry, Result;

  sev_seg_hex_decoder sev_seg_hex_decoder_1 (
    .BCD(A), .a(sev_seg_hex_decoder_1_a), .b(sev_seg_hex_decoder_1_b), .c(sev_seg_hex_decoder_1_c),
    .d(sev_seg_hex_decoder_1_d), .e(sev_seg_hex_decoder_1_e), .f(sev_seg_hex_decoder_1_f),
    .g(sev_seg_hex_decoder_1_g), .dec(sev_seg_hex_decoder_1_dec));  // open: NEG
  sev_seg_hex_decoder sev_seg_hex_decoder_3 (
    .BCD(B), .a(sev_seg_hex_decoder_3_a), .b(sev_seg_hex_decoder_3_b), .c(sev_seg_hex_decoder_3_c),
    .d(sev_seg_hex_decoder_3_d), .e(sev_seg_hex_decoder_3_e), .f(sev_seg_hex_decoder_3_f),
    .g(sev_seg_hex_decoder_3_g), .dec(sev_seg_hex_decoder_3_dec));  // open: NEG
  _7_Segment_Display #(.active("false")) L_7_Segment_Display_1 (
    .g(sev_seg_hex_decoder_1_g), .f(sev_seg_hex_decoder_1_f), .a(sev_seg_hex_decoder_1_a),
    .b(sev_seg_hex_decoder_1_b), .e(sev_seg_hex_decoder_1_e), .d(sev_seg_hex_decoder_1_d),
    .c(sev_seg_hex_decoder_1_c), .dp(sev_seg_hex_decoder_1_dec));
  _7_Segment_Display #(.active("false")) L_7_Segment_Display_4 (
    .g(sev_seg_hex_decoder_3_g), .f(sev_seg_hex_decoder_3_f), .a(sev_seg_hex_decoder_3_a),
    .b(sev_seg_hex_decoder_3_b), .e(sev_seg_hex_decoder_3_e), .d(sev_seg_hex_decoder_3_d),
    .c(sev_seg_hex_decoder_3_c), .dp(sev_seg_hex_decoder_3_dec));
  Decoder #(.select(2)) decoder_1 (.out1(SUB), .sel(Oper_S));  // open: out0, out2, out3, en
  and and_1 (Neg_LED, SUB, Carry[0]);
  ALU_ASAO ALU_ASAO_1 (.A(A), .B(B), .Oper_S(Oper_S), .Carry(Carry), .Result(Result));
  sev_seg_hex_decoder sev_seg_hex_decoder_2 (
    .BCD(Carry), .NEG(Neg_LED), .a(sev_seg_hex_decoder_2_a), .b(sev_seg_hex_decoder_2_b),
    .c(sev_seg_hex_decoder_2_c), .d(sev_seg_hex_decoder_2_d), .e(sev_seg_hex_decoder_2_e),
    .f(sev_seg_hex_decoder_2_f), .g(sev_seg_hex_decoder_2_g), .dec(sev_seg_hex_decoder_2_dec));
  _7_Segment_Display #(.active("false")) L_7_Segment_Display_2 (
    .g(sev_seg_hex_decoder_2_g), .f(sev_seg_hex_decoder_2_f), .a(sev_seg_hex_decoder_2_a),
    .b(sev_seg_hex_decoder_2_b), .e(sev_seg_hex_decoder_2_e), .d(sev_seg_hex_decoder_2_d),
    .c(sev_seg_hex_decoder_2_c), .dp(sev_seg_hex_decoder_2_dec));
  _7_Segment_Display #(.active("false")) L_7_Segment_Display_3 (
    .g(sev_seg_hex_decoder_4_g), .f(sev_seg_hex_decoder_4_f), .a(sev_seg_hex_decoder_4_a),
    .b(sev_seg_hex_decoder_4_b), .e(sev_seg_hex_decoder_4_e), .d(sev_seg_hex_decoder_4_d),
    .c(sev_seg_hex_decoder_4_c), .dp(sev_seg_hex_decoder_4_dec));
  sev_seg_hex_decoder sev_seg_hex_decoder_4 (
    .BCD(Result), .a(sev_seg_hex_decoder_4_a), .b(sev_seg_hex_decoder_4_b), .c(sev_seg_hex_decoder_4_c),
    .d(sev_seg_hex_decoder_4_d), .e(sev_seg_hex_decoder_4_e), .f(sev_seg_hex_decoder_4_f),
    .g(sev_seg_hex_decoder_4_g), .dec(sev_seg_hex_decoder_4_dec));  // open: NEG

  // Other names for the same wires on the sheet: NEG = Neg_LED

  // Notes on the sheet:
  //   (Over 15)
  //   TODO: Figure out Carry out logic
endmodule

module FA (
  input  C_in,
  input  A,
  input  B,
  output Sum,
  output C_out
);

  wire and_1_out, and_2_out, and_3_out, and_4_out, and_5_out, and_6_out, and_7_out, not_1_out, not_2_out,
       not_3_out;

  not not_1 (not_1_out, C_in);
  not not_2 (not_2_out, A);
  not not_3 (not_3_out, B);
  and and_1 (and_1_out, not_1_out, not_2_out, B);
  and and_2 (and_2_out, not_1_out, A, not_3_out);
  and and_3 (and_3_out, C_in, not_2_out, not_3_out);
  and and_4 (and_4_out, C_in, A, B);
  and and_5 (and_5_out, A, B);
  and and_6 (and_6_out, C_in, B);
  and and_7 (and_7_out, C_in, A);
  or or_1 (Sum, and_1_out, and_2_out, and_3_out, and_4_out);
  or or_2 (C_out, and_5_out, and_6_out, and_7_out);
endmodule

module RC_AS (
  input  [3:0] x,
  input  [3:0] y,
  input  Sub,
  output [3:0] z,
  output C_out
);

  wire FA_1_c_out, FA_2_c_out, FA_3_c_out, y0, y1, y2, y3;

  xor xor_1 (y3, Sub, y[3]);
  xor xor_2 (y2, Sub, y[2]);
  xor xor_3 (y1, y[1], Sub);
  xor xor_4 (y0, y[0], Sub);
  FA FA_1 (.C_in(Sub), .A(x[0]), .B(y0), .Sum(z[0]), .C_out(FA_1_c_out));
  FA FA_2 (.C_in(FA_1_c_out), .A(x[1]), .B(y1), .Sum(z[1]), .C_out(FA_2_c_out));
  FA FA_3 (.C_in(FA_2_c_out), .A(x[2]), .B(y2), .Sum(z[2]), .C_out(FA_3_c_out));
  FA FA_4 (.C_in(FA_3_c_out), .A(x[3]), .B(y3), .Sum(z[3]), .C_out(C_out));

  // Other names for the same wires on the sheet: AS = Sub
endmodule

module ALU_ASAO (
  input  [3:0] A,
  input  [3:0] B,
  input  [1:0] Oper_S,
  output [3:0] Carry,
  output [3:0] Result
);

  wire ADD_Carry, RC_AS_2_c_out, SUB_Carry;
  wire [3:0] ADD, ADD_c_BCD, AN, ORR, SUB, SUB_c_BCD;

  assign AN = A & B;  // AND_Gate and_1, 4 bits wide
  assign ORR = A | B;  // OR_Gate or_1, 4 bits wide
  Multiplexer #(.select(2), .width(4)) multiplexer_1 (
    .in0(ADD), .in1(SUB), .in2(AN), .in3(ORR), .out(Result), .sel(Oper_S));
  RC_AS RC_AS_1 (.x(A), .y(B), .Sub(1'b0), .z(ADD), .C_out(ADD_Carry));
  RC_AS RC_AS_2 (.x(A), .y(B), .Sub(1'b1), .z(SUB), .C_out(RC_AS_2_c_out));
  not not_1 (SUB_Carry, RC_AS_2_c_out);
  Multiplexer #(.select(2), .width(4)) multiplexer_2 (
    .in0(ADD_c_BCD), .in1(SUB_c_BCD), .in2(4'b0000), .in3(4'b0000), .out(Carry), .sel(Oper_S));
  carry2BCD carry2BCD_1 (.C_in(ADD_Carry), .C_out_BCD(ADD_c_BCD));
  carry2BCD carry2BCD_2 (.C_in(SUB_Carry), .C_out_BCD(SUB_c_BCD));

  // Notes on the sheet:
  //   ADD
  //   SUB
endmodule

module carry2BCD (
  input  C_in,
  output [3:0] C_out_BCD
);


  assign C_out_BCD = {3'b000, C_in};
endmodule

module sev_seg_hex_decoder (
  input  [3:0] BCD,
  input  NEG,
  output a,
  output b,
  output c,
  output d,
  output e,
  output f,
  output g,
  output dec
);

  wire and_1_out, and_2_out, and_3_out, and_4_out, and_5_out, and_6_out, and_7_out, and_8_out, and_9_out,
       and_10_out, and_11_out, and_12_out, and_13_out, and_14_out, and_15_out, and_16_out, and_17_out,
       and_18_out, and_19_out, and_20_out, and_21_out, and_22_out, and_23_out, and_24_out, and_25_out,
       not_1_out, not_2_out, not_3_out, not_4_out;
  wire [6:0] Norm;

  not not_1 (not_1_out, BCD[3]);
  not not_2 (not_2_out, BCD[2]);
  not not_3 (not_3_out, BCD[1]);
  not not_4 (not_4_out, BCD[0]);
  and and_1 (and_1_out, not_1_out, not_2_out, not_3_out, BCD[0]);
  and and_2 (and_2_out, not_1_out, BCD[2], not_3_out, not_4_out);
  and and_3 (and_3_out, BCD[3], not_2_out, BCD[1], BCD[0]);
  and and_4 (and_4_out, BCD[3], BCD[2], not_3_out, BCD[0]);
  and and_5 (and_5_out, not_1_out, BCD[2], not_3_out, BCD[0]);
  and and_6 (and_6_out, BCD[2], BCD[1], not_4_out);
  and and_7 (and_7_out, BCD[3], BCD[1], BCD[0]);
  and and_8 (and_8_out, BCD[3], BCD[2], not_4_out);
  and and_9 (and_9_out, not_1_out, not_2_out, BCD[1], not_4_out);
  and and_10 (and_10_out, BCD[3], BCD[2], not_4_out);
  and and_11 (and_11_out, BCD[3], BCD[2], BCD[1]);
  and and_12 (and_12_out, not_1_out, not_2_out, not_3_out, BCD[0]);
  and and_13 (and_13_out, not_1_out, BCD[2], not_3_out, not_4_out);
  and and_14 (and_14_out, BCD[2], BCD[1], BCD[0]);
  and and_15 (and_15_out, BCD[3], not_2_out, BCD[1], not_4_out);
  and and_16 (and_16_out, not_1_out, BCD[0]);
  and and_17 (and_17_out, not_1_out, BCD[2], not_3_out);
  and and_18 (and_18_out, not_2_out, not_3_out, BCD[0]);
  and and_19 (and_19_out, not_1_out, not_2_out, BCD[0]);
  and and_20 (and_20_out, not_1_out, not_2_out, BCD[1]);
  and and_21 (and_21_out, not_1_out, BCD[1], BCD[0]);
  and and_22 (and_22_out, BCD[3], BCD[2], not_3_out, BCD[0]);
  and and_23 (and_23_out, not_1_out, not_2_out, not_3_out);
  and and_24 (and_24_out, not_1_out, BCD[2], BCD[1], BCD[0]);
  and and_25 (and_25_out, BCD[3], BCD[2], not_3_out, not_4_out);
  or or_1 (Norm[0], and_1_out, and_2_out, and_3_out, and_4_out);
  or or_2 (Norm[1], and_5_out, and_6_out, and_7_out, and_8_out);
  or or_3 (Norm[2], and_9_out, and_10_out, and_11_out);
  or or_4 (Norm[3], and_12_out, and_13_out, and_14_out, and_15_out);
  or or_5 (Norm[4], and_16_out, and_17_out, and_18_out);
  or or_6 (Norm[5], and_19_out, and_20_out, and_21_out, and_22_out);
  or or_7 (Norm[6], and_23_out, and_24_out, and_25_out);
  Multiplexer #(.width(8)) multiplexer_1 (.in0({1'b1, Norm}), .in1(8'hbf), .out({dec, g, f, e, d, c, b, a}), .sel(NEG));
endmodule
