// Logisim project BCD_AS_7seg.circ as structural Verilog: 9 circuits, main circuit main
module main (
  input  [3:0] X,
  input  [3:0] Y,
  input  AS,
  output [3:0] Z_out,
  output carrrrr,
  output [6:0] Z_2,
  output [6:0] Z_0,
  output [6:0] Z_1
);

  RC_AS RC_AS_1 (.x(X), .y(Y), .AS(AS), .z_out(Z_out), .carry_out(carrrrr));
  sev_segment_decoder sev_segment_decoder_2 (
    .Input_4bits(X), .a(Z_0[0]), .b(Z_0[1]), .c(Z_0[2]), .d(Z_0[3]), .e(Z_0[4]), .f(Z_0[5]), .g(Z_0[6]));  // open: bus_out
  sev_segment_decoder sev_segment_decoder_3 (
    .Input_4bits(Y), .a(Z_1[0]), .b(Z_1[1]), .c(Z_1[2]), .d(Z_1[3]), .e(Z_1[4]), .f(Z_1[5]), .g(Z_1[6]));  // open: bus_out
  sev_segment_decoder sev_segment_decoder_1 (
    .Input_4bits(Z_out), .a(Z_2[0]), .b(Z_2[1]), .c(Z_2[2]), .d(Z_2[3]), .e(Z_2[4]), .f(Z_2[5]), .g(Z_2[6]));  // open: bus_out
endmodule

module sev_segment_decoder (
  input  [3:0] Input_4bits,
  output a,
  output b,
  output c,
  output d,
  output e,
  output f,
  output g,
  output [6:0] bus_out
);

  wire and_1_out, and_2_out, and_3_out, and_4_out, and_5_out, and_6_out, and_7_out, and_8_out, and_9_out,
       and_10_out, and_11_out, and_12_out, and_13_out, and_14_out, and_15_out, and_16_out, and_17_out,
       and_18_out, and_19_out, and_20_out, and_21_out, and_22_out, and_23_out, and_24_out, and_25_out,
       not_1_out, not_2_out, not_3_out, not_4_out;

  not not_1 (not_1_out, Input_4bits[3]);
  not not_2 (not_2_out, Input_4bits[2]);
  not not_3 (not_3_out, Input_4bits[1]);
  not not_4 (not_4_out, Input_4bits[0]);
  and and_1 (and_1_out, not_1_out, not_2_out, not_3_out, Input_4bits[0]);
  and and_2 (and_2_out, not_1_out, Input_4bits[2], not_3_out, not_4_out);
  and and_3 (and_3_out, Input_4bits[3], not_2_out, Input_4bits[1], Input_4bits[0]);
  and and_4 (and_4_out, Input_4bits[3], Input_4bits[2], not_3_out, Input_4bits[0]);
  and and_5 (and_5_out, not_1_out, Input_4bits[2], not_3_out, Input_4bits[0]);
  and and_6 (and_6_out, Input_4bits[2], Input_4bits[1], not_4_out);
  and and_7 (and_7_out, Input_4bits[3], Input_4bits[1], Input_4bits[0]);
  and and_8 (and_8_out, Input_4bits[3], Input_4bits[2], not_4_out);
  and and_9 (and_9_out, not_1_out, not_2_out, Input_4bits[1], not_4_out);
  and and_10 (and_10_out, Input_4bits[3], Input_4bits[2], not_4_out);
  and and_11 (and_11_out, Input_4bits[3], Input_4bits[2], Input_4bits[1]);
  and and_12 (and_12_out, not_1_out, not_2_out, not_3_out, Input_4bits[0]);
  and and_13 (and_13_out, not_1_out, Input_4bits[2], not_3_out, not_4_out);
  and and_14 (and_14_out, Input_4bits[2], Input_4bits[1], Input_4bits[0]);
  and and_15 (and_15_out, Input_4bits[3], not_2_out, Input_4bits[1], not_4_out);
  and and_16 (and_16_out, not_1_out, Input_4bits[0]);
  and and_17 (and_17_out, not_1_out, Input_4bits[2], not_3_out);
  and and_18 (and_18_out, not_2_out, not_3_out, Input_4bits[0]);
  and and_19 (and_19_out, not_1_out, not_2_out, Input_4bits[0]);
  and and_20 (and_20_out, not_1_out, not_2_out, Input_4bits[1]);
  and and_21 (and_21_out, not_1_out, Input_4bits[1], Input_4bits[0]);
  and and_22 (and_22_out, Input_4bits[3], Input_4bits[2], not_3_out, Input_4bits[0]);
  and and_23 (and_23_out, not_1_out, not_2_out, not_3_out);
  and and_24 (and_24_out, not_1_out, Input_4bits[2], Input_4bits[1], Input_4bits[0]);
  and and_25 (and_25_out, Input_4bits[3], Input_4bits[2], not_3_out, not_4_out);
  or or_1 (a, and_1_out, and_2_out, and_3_out, and_4_out);
  or or_2 (b, and_5_out, and_6_out, and_7_out, and_8_out);
  or or_3 (bus_out[2], and_9_out, and_10_out, and_11_out);
  or or_4 (bus_out[3], and_12_out, and_13_out, and_14_out, and_15_out);
  or or_5 (bus_out[4], and_16_out, and_17_out, and_18_out);
  or or_6 (bus_out[5], and_19_out, and_20_out, and_21_out, and_22_out);
  or or_7 (bus_out[6], and_23_out, and_24_out, and_25_out);

  assign bus_out[1:0] = {b, a};
  assign c = bus_out[2];
  assign d = bus_out[3];
  assign e = bus_out[4];
  assign f = bus_out[5];
  assign g = bus_out[6];
endmodule

module Full_adder (
  input  A,
  input  B,
  input  C,
  output sum,
  output carry
);

  wire and_1_out, and_2_out, and_3_out, and_4_out, and_5_out, and_6_out, and_7_out, not_1_out, not_2_out,
       not_3_out;

  not not_1 (not_1_out, A);
  not not_2 (not_2_out, B);
  not not_3 (not_3_out, C);
  and and_1 (and_1_out, not_1_out, not_2_out, C);
  and and_2 (and_2_out, not_1_out, B, not_3_out);
  and and_3 (and_3_out, A, not_2_out, not_3_out);
  and and_4 (and_4_out, A, B, C);
  and and_5 (and_5_out, B, C);
  and and_6 (and_6_out, A, C);
  or or_1 (carry, and_5_out, and_6_out, and_7_out);
  and and_7 (and_7_out, A, B);
  or or_2 (sum, and_1_out, and_2_out, and_3_out, and_4_out);
endmodule

module RC_AS (
  input  [3:0] x,
  input  [3:0] y,
  input  AS,
  output [3:0] z_out,
  output carry_out
);

  wire Full_adder_1_carry, Full_adder_2_carry, Full_adder_3_carry, Full_adder_4_carry, y0, y1, y2, y3;

  xor xor_1 (y0, AS, y[0]);
  xor xor_2 (y1, AS, y[1]);
  xor xor_3 (y2, AS, y[2]);
  xor xor_4 (y3, AS, y[3]);
  Full_adder Full_adder_1 (.A(x[0]), .B(y0), .C(AS), .sum(z_out[0]), .carry(Full_adder_1_carry));
  Full_adder Full_adder_2 (.A(x[1]), .B(y1), .C(Full_adder_1_carry), .sum(z_out[1]), .carry(Full_adder_2_carry));
  Full_adder Full_adder_3 (.A(x[2]), .B(y2), .C(Full_adder_2_carry), .sum(z_out[2]), .carry(Full_adder_3_carry));
  Full_adder Full_adder_4 (.A(x[3]), .B(y3), .C(Full_adder_3_carry), .sum(z_out[3]), .carry(Full_adder_4_carry));
  not not_1 (carry_out, Full_adder_4_carry);

  // Other names for the same wires on the sheet: z0 = z_out[0]; z1 = z_out[1]; z2 = z_out[2]; z3 = z_out[3]
endmodule

module overflow (
  input  [3:0] bits_in,
  output [3:0] Carr_out,
  output [3:0] BCD_out
);

  wire and_1_out, and_2_out, and_4_out, and_5_out, and_6_out, and_7_out, not_1_out, not_2_out, not_3_out;

  not not_1 (not_1_out, bits_in[3]);
  not not_2 (not_2_out, bits_in[2]);
  not not_3 (not_3_out, bits_in[1]);
  and and_1 (and_1_out, bits_in[3], bits_in[1]);
  and and_2 (and_2_out, bits_in[3], bits_in[2]);
  and and_3 (BCD_out[3], bits_in[3], not_2_out, not_3_out);
  and and_4 (and_4_out, not_1_out, bits_in[2]);
  and and_5 (and_5_out, bits_in[2], bits_in[1]);
  and and_6 (and_6_out, not_1_out, bits_in[1]);
  and and_7 (and_7_out, bits_in[3], bits_in[2], not_3_out);
  or or_1 (Carr_out[0], and_1_out, and_2_out);
  or or_2 (BCD_out[2], and_4_out, and_5_out);
  or or_3 (BCD_out[1], and_6_out, and_7_out);

  assign BCD_out[0] = bits_in[0];
  assign Carr_out[3:1] = 3'b000;
endmodule

module BCD (
  input  [3:0] x1,
  input  [3:0] x0,
  input  [3:0] y1,
  input  [3:0] y0,
  output [3:0] LSBs,
  output [3:0] MSBs,
  output [3:0] Carry_out
);

  wire [3:0] overflow_1_carr_out, overflow_2_bcd_out, RC_AS_1_z_out, RC_AS_2_z_out;

  RC_AS RC_AS_1 (.x(x0), .y(y0), .AS(1'b0), .z_out(RC_AS_1_z_out));  // open: carry_out
  RC_AS RC_AS_2 (.x(x1), .y(y1), .AS(1'b0), .z_out(RC_AS_2_z_out));  // open: carry_out
  overflow overflow_1 (.bits_in(RC_AS_1_z_out), .Carr_out(overflow_1_carr_out), .BCD_out(LSBs));
  overflow overflow_2 (.bits_in(RC_AS_2_z_out), .Carr_out(Carry_out), .BCD_out(overflow_2_bcd_out));
  RC_AS RC_AS_3 (.x(overflow_1_carr_out), .y(overflow_2_bcd_out), .AS(1'b0), .z_out(MSBs));  // open: carry_out
endmodule

module BCD_Adder_w_displaysd (
  input  [3:0] x1,
  input  [3:0] x0,
  input  [3:0] y0,
  input  [3:0] y1,
  output C_out_1
);

  wire a, b, f, g, sev_segment_decoder_1_a, sev_segment_decoder_1_b, sev_segment_decoder_1_c,
       sev_segment_decoder_1_d, sev_segment_decoder_1_e, sev_segment_decoder_1_f, sev_segment_decoder_1_g,
       sev_segment_decoder_2_a, sev_segment_decoder_2_b, sev_segment_decoder_2_c, sev_segment_decoder_2_d,
       sev_segment_decoder_2_e, sev_segment_decoder_2_f, sev_segment_decoder_2_g, sev_segment_decoder_3_a,
       sev_segment_decoder_3_b, sev_segment_decoder_3_c, sev_segment_decoder_3_d, sev_segment_decoder_3_e,
       sev_segment_decoder_3_f, sev_segment_decoder_3_g, sev_segment_decoder_4_c, sev_segment_decoder_4_d,
       sev_segment_decoder_4_e, sev_segment_decoder_5_a, sev_segment_decoder_5_b, sev_segment_decoder_5_c,
       sev_segment_decoder_5_d, sev_segment_decoder_5_e, sev_segment_decoder_5_f, sev_segment_decoder_5_g,
       sev_segment_decoder_6_a, sev_segment_decoder_6_b, sev_segment_decoder_6_c, sev_segment_decoder_6_d,
       sev_segment_decoder_6_e, sev_segment_decoder_6_f, sev_segment_decoder_6_g, sev_segment_decoder_7_a,
       sev_segment_decoder_7_b, sev_segment_decoder_7_c, sev_segment_decoder_7_d, sev_segment_decoder_7_e,
       sev_segment_decoder_7_f, sev_segment_decoder_7_g;
  wire [2:0] BCD_1_carry_out;
  wire [3:0] BCD_1_lsbs, BCD_1_msbs;

  sev_segment_decoder sev_segment_decoder_3 (
    .Input_4bits(x1), .a(sev_segment_decoder_3_a), .b(sev_segment_decoder_3_b), .c(sev_segment_decoder_3_c),
    .d(sev_segment_decoder_3_d), .e(sev_segment_decoder_3_e), .f(sev_segment_decoder_3_f),
    .g(sev_segment_decoder_3_g));  // open: bus_out
  sev_segment_decoder sev_segment_decoder_6 (
    .Input_4bits(y1), .a(sev_segment_decoder_6_a), .b(sev_segment_decoder_6_b), .c(sev_segment_decoder_6_c),
    .d(sev_segment_decoder_6_d), .e(sev_segment_decoder_6_e), .f(sev_segment_decoder_6_f),
    .g(sev_segment_decoder_6_g));  // open: bus_out
  _7_Segment_Display #(.active("false")) x1_seg (
    .g(sev_segment_decoder_3_g), .f(sev_segment_decoder_3_f), .a(sev_segment_decoder_3_a),
    .b(sev_segment_decoder_3_b), .e(sev_segment_decoder_3_e), .d(sev_segment_decoder_3_d),
    .c(sev_segment_decoder_3_c));  // open: dp
  _7_Segment_Display #(.active("false")) x0_seg (
    .g(sev_segment_decoder_5_g), .f(sev_segment_decoder_5_f), .a(sev_segment_decoder_5_a),
    .b(sev_segment_decoder_5_b), .e(sev_segment_decoder_5_e), .d(sev_segment_decoder_5_d),
    .c(sev_segment_decoder_5_c));  // open: dp
  _7_Segment_Display #(.active("false")) y1_seg (
    .g(sev_segment_decoder_6_g), .f(sev_segment_decoder_6_f), .a(sev_segment_decoder_6_a),
    .b(sev_segment_decoder_6_b), .e(sev_segment_decoder_6_e), .d(sev_segment_decoder_6_d),
    .c(sev_segment_decoder_6_c));  // open: dp
  _7_Segment_Display #(.active("false")) y0_seg (
    .g(sev_segment_decoder_7_g), .f(sev_segment_decoder_7_f), .a(sev_segment_decoder_7_a),
    .b(sev_segment_decoder_7_b), .e(sev_segment_decoder_7_e), .d(sev_segment_decoder_7_d),
    .c(sev_segment_decoder_7_c));  // open: dp
  sev_segment_decoder sev_segment_decoder_5 (
    .Input_4bits(x0), .a(sev_segment_decoder_5_a), .b(sev_segment_decoder_5_b), .c(sev_segment_decoder_5_c),
    .d(sev_segment_decoder_5_d), .e(sev_segment_decoder_5_e), .f(sev_segment_decoder_5_f),
    .g(sev_segment_decoder_5_g));  // open: bus_out
  sev_segment_decoder sev_segment_decoder_7 (
    .Input_4bits(y0), .a(sev_segment_decoder_7_a), .b(sev_segment_decoder_7_b), .c(sev_segment_decoder_7_c),
    .d(sev_segment_decoder_7_d), .e(sev_segment_decoder_7_e), .f(sev_segment_decoder_7_f),
    .g(sev_segment_decoder_7_g));  // open: bus_out
  BCD BCD_1 (
    .x1(x1), .x0(x0), .y1(y0), .y0(y1), .LSBs(BCD_1_lsbs), .MSBs(BCD_1_msbs),
    .Carry_out({BCD_1_carry_out, C_out_1}));
  sev_segment_decoder sev_segment_decoder_1 (
    .Input_4bits({BCD_1_carry_out, C_out_1}), .a(sev_segment_decoder_1_a), .b(sev_segment_decoder_1_b),
    .c(sev_segment_decoder_1_c), .d(sev_segment_decoder_1_d), .e(sev_segment_decoder_1_e),
    .f(sev_segment_decoder_1_f), .g(sev_segment_decoder_1_g));  // open: bus_out
  _7_Segment_Display #(.active("false")) c_out_seg (
    .g(sev_segment_decoder_1_g), .f(sev_segment_decoder_1_f), .a(sev_segment_decoder_1_a),
    .b(sev_segment_decoder_1_b), .e(sev_segment_decoder_1_e), .d(sev_segment_decoder_1_d),
    .c(sev_segment_decoder_1_c));  // open: dp
  sev_segment_decoder sev_segment_decoder_4 (
    .Input_4bits(BCD_1_msbs), .a(a), .b(b), .c(sev_segment_decoder_4_c), .d(sev_segment_decoder_4_d),
    .e(sev_segment_decoder_4_e), .f(f), .g(g));  // open: bus_out
  _7_Segment_Display #(.active("false")) z1_seg (
    .g(g), .f(f), .a(a), .b(b), .e(sev_segment_decoder_4_e), .d(sev_segment_decoder_4_d),
    .c(sev_segment_decoder_4_c));  // open: dp
  _7_Segment_Display #(.active("false")) z0_seg (
    .g(sev_segment_decoder_2_g), .f(sev_segment_decoder_2_f), .a(sev_segment_decoder_2_a),
    .b(sev_segment_decoder_2_b), .e(sev_segment_decoder_2_e), .d(sev_segment_decoder_2_d),
    .c(sev_segment_decoder_2_c));  // open: dp
  sev_segment_decoder sev_segment_decoder_2 (
    .Input_4bits(BCD_1_lsbs), .a(sev_segment_decoder_2_a), .b(sev_segment_decoder_2_b),
    .c(sev_segment_decoder_2_c), .d(sev_segment_decoder_2_d), .e(sev_segment_decoder_2_e),
    .f(sev_segment_decoder_2_f), .g(sev_segment_decoder_2_g));  // open: bus_out
endmodule

module regsiters (
  input  A_en,
  input  [7:0] Input_bus,
  input  B_en,
  input  Reset,
  output [3:0] A_tens,
  output [3:0] A_ones,
  output [3:0] B_tens,
  output [3:0] B_ones
);

  wire clock_in_out, not_1_out, not_2_out;

  not not_1 (not_1_out, A_en);
  Clock clock_in (.out(clock_in_out));
  not not_2 (not_2_out, B_en);
  Register OperA (.D(Input_bus), .en(not_1_out), .clk(clock_in_out), .Q({A_tens, A_ones}), .clr(Reset));
  Register OperB (.D(Input_bus), .en(not_2_out), .clk(clock_in_out), .Q({B_tens, B_ones}), .clr(Reset));
endmodule

module BCD_w_registers (
  input  Key1,
  input  [7:0] Input_bus,
  input  Key2,
  input  Input_1,
  output [6:0] LSBs,
  output [6:0] MSBs,
  output [6:0] x1,
  output [6:0] x0,
  output [3:0] Carry,
  output [6:0] y1,
  output [6:0] y0
);

  wire [3:0] A_ones, A_tens, B_ones, B_tens, Z_carry, Z_ones, Z_tens;

  // BCD_to_7_Segment_decoder bcd_to_7_segment_decoder_1: pin names not known; wires that end beside it: A_tens
  _7_Segment_Display L_7_Segment_Display_1 ();  // open: g, f, a, b, e, d, c, dp
  sev_segment_decoder sev_segment_decoder_3 (.Input_4bits(A_tens), .bus_out(x1));  // open: a, b, c, d, e, f, g
  // BCD_to_7_Segment_decoder bcd_to_7_segment_decoder_2: pin names not known; wires that end beside it: A_ones
  _7_Segment_Display L_7_Segment_Display_2 ();  // open: g, f, a, b, e, d, c, dp
  sev_segment_decoder sev_segment_decoder_6 (.Input_4bits(B_tens), .bus_out(y1));  // open: a, b, c, d, e, f, g
  regsiters regsiters_1 (
    .A_en(Key1), .Input_bus(Input_bus), .B_en(Key2), .Reset(Input_1), .A_tens(A_tens), .A_ones(A_ones),
    .B_tens(B_tens), .B_ones(B_ones));
  // BCD_to_7_Segment_decoder bcd_to_7_segment_decoder_3: pin names not known; wires that end beside it: B_tens
  _7_Segment_Display L_7_Segment_Display_3 ();  // open: g, f, a, b, e, d, c, dp
  // BCD_to_7_Segment_decoder bcd_to_7_segment_decoder_4: pin names not known; wires that end beside it: B_ones
  _7_Segment_Display L_7_Segment_Display_4 ();  // open: g, f, a, b, e, d, c, dp
  sev_segment_decoder sev_segment_decoder_4 (.Input_4bits(A_ones), .bus_out(x0));  // open: a, b, c, d, e, f, g
  sev_segment_decoder sev_segment_decoder_7 (.Input_4bits(B_ones), .bus_out(y0));  // open: a, b, c, d, e, f, g
  // BCD_to_7_Segment_decoder bcd_to_7_segment_decoder_5: pin names not known; wires that end beside it: Z_carry
  _7_Segment_Display L_7_Segment_Display_5 ();  // open: g, f, a, b, e, d, c, dp
  BCD BCD_1 (.x1(A_tens), .x0(A_ones), .y1(B_tens), .y0(B_ones), .LSBs(Z_ones), .MSBs(Z_tens), .Carry_out(Z_carry));
  // BCD_to_7_Segment_decoder bcd_to_7_segment_decoder_6: pin names not known; wires that end beside it: Z_tens
  _7_Segment_Display L_7_Segment_Display_6 ();  // open: g, f, a, b, e, d, c, dp
  assign Carry = ~Z_carry;  // NOT_Gate not_1, 4 bits wide
  // BCD_to_7_Segment_decoder bcd_to_7_segment_decoder_7: pin names not known; wires that end beside it: Z_ones
  _7_Segment_Display L_7_Segment_Display_7 ();  // open: g, f, a, b, e, d, c, dp
  sev_segment_decoder sev_segment_decoder_1 (.Input_4bits(Z_ones), .bus_out(LSBs));  // open: a, b, c, d, e, f, g
  sev_segment_decoder sev_segment_decoder_2 (.Input_4bits(Z_tens), .bus_out(MSBs));  // open: a, b, c, d, e, f, g

  // Notes on the sheet:
  //   +
  //   =
endmodule
