// Logisim project Self_Adders.circ as structural Verilog
module FA (
  input  x,
  input  y,
  input  C_in,
  output sum,
  output C_out
);

  wire and_1_out, and_2_out, and_3_out, and_4_out, and_5_out, and_6_out, and_7_out, not_1_out, not_2_out,
       not_3_out;

  not not_1 (not_1_out, x);
  not not_2 (not_2_out, y);
  not not_3 (not_3_out, C_in);
  and and_1 (and_1_out, not_1_out, not_2_out, C_in);
  and and_2 (and_2_out, not_1_out, y, not_3_out);
  and and_3 (and_3_out, x, not_2_out, not_3_out);
  and and_4 (and_4_out, x, y, C_in);
  and and_5 (and_5_out, y, C_in);
  and and_6 (and_6_out, x, C_in);
  and and_7 (and_7_out, x, y);
  or or_1 (sum, and_1_out, and_2_out, and_3_out, and_4_out);
  or or_2 (C_out, and_5_out, and_6_out, and_7_out);
endmodule

module RC_4bits (
  input  [3:0] x,
  input  [3:0] y,
  input  C_in,
  output [3:0] Sum,
  output C_out
);

  wire fa_1_c_out, fa_2_c_out, fa_3_c_out;

  FA fa_1 (.x(x[0]), .y(y[0]), .C_in(C_in), .sum(Sum[0]), .C_out(fa_1_c_out));
  FA fa_2 (.x(x[1]), .y(y[1]), .C_in(fa_1_c_out), .sum(Sum[1]), .C_out(fa_2_c_out));
  FA fa_3 (.x(x[2]), .y(y[2]), .C_in(fa_2_c_out), .sum(Sum[2]), .C_out(fa_3_c_out));
  FA fa_4 (.x(x[3]), .y(y[3]), .C_in(fa_3_c_out), .sum(Sum[3]), .C_out(C_out));

  // Other names for the same wires on the sheet: z0 = Sum[0]; z1 = Sum[1]; z2 = Sum[2]; z3 = Sum[3]
endmodule

module ALU_AS (
  input  s,
  input  [3:0] B,
  input  [3:0] A,
  input  C_in,
  output [3:0] Sum,
  output C_out
);

  wire [3:0] xor_4_out;

  xor xor_1 (xor_4_out[3], s, B[3]);
  xor xor_2 (xor_4_out[2], s, B[2]);
  xor xor_3 (xor_4_out[1], s, B[1]);
  xor xor_4 (xor_4_out[0], s, B[0]);
  RC_4bits rc_4bits_1 (.x(A), .y(xor_4_out), .C_in(C_in), .Sum(Sum), .C_out(C_out));
endmodule
